// Logisim project jsw50_HW3_3a.circ as structural Verilog: 1 circuit, main circuit jsw50_3a
module jsw50_3a (
  input  A,
  input  B,
  input  C,
  output out_4
);

  wire and_1_out, and_2_out, not_1_out, not_2_out, or_1_out;

  and and_1 (and_1_out, A, B);
  or or_1 (or_1_out, A, B);
  not not_1 (not_1_out, or_1_out);
  not not_2 (not_2_out, C);
  and and_2 (and_2_out, not_1_out, C);
  or or_2 (out_4, and_1_out, and_2_out, not_2_out);
endmodule
