// Logisim project jsw50_HW3_3c.circ as structural Verilog: 1 circuit, main circuit main
module main (
  input  In2,
  input  In1,
  input  In0,
  output out_4
);

  wire and_2_out, and_3_out, and_4_out, and_5_out, button_1_out, not_1_out, not_2_out, not_3_out, not_4_out,
       not_5_out, not_6_out, not_7_out, not_8_out, or_1_out, or_2_out, Q0, Q0not, Q1, Q1not;

  not not_1 (not_1_out, In1);
  not not_2 (not_2_out, In2);
  not not_3 (not_3_out, In1);
  not not_4 (not_4_out, In2);
  not not_5 (not_5_out, In0);
  and and_1 (out_4, In2, not_1_out, In0, Q1, Q0);
  and and_2 (and_2_out, not_2_out, not_3_out, In0, Q1not, Q0not);
  and and_3 (and_3_out, not_4_out, In1, not_5_out, Q1, Q0not);
  Button button_1 (.out(button_1_out));
  or or_1 (or_1_out, and_2_out, and_3_out);
  not not_6 (not_6_out, In2);
  D_Flip_Flop u_Q0 (.clk(button_1_out), .D(or_1_out), .Q(Q0), .Qn(Q0not));  // open: preset, en, reset
  and and_4 (and_4_out, not_6_out, In1, In0, Q1not, Q0);
  not not_7 (not_7_out, In2);
  not not_8 (not_8_out, In0);
  and and_5 (and_5_out, not_7_out, In1, not_8_out, Q1, Q0not);
  or or_2 (or_2_out, and_4_out, and_5_out);
  D_Flip_Flop u_Q1 (.clk(button_1_out), .D(or_2_out), .Q(Q1), .Qn(Q1not));  // open: preset, en, reset

  // Notes on the sheet:
  //   Mealy-style Machine
endmodule
