// Logisim project jsw50_HW3_3d.circ as structural Verilog: 1 circuit, main circuit main
module main (
  input  In1,
  input  In0,
  output out_3
);

  wire and_1_out, and_2_out, and_3_out, and_4_out, and_5_out, and_6_out, and_7_out, and_8_out, and_9_out,
       and_10_out, and_11_out, and_12_out, and_13_out, and_14_out, and_15_out, and_16_out, and_17_out,
       and_18_out, and_19_out, and_20_out, and_21_out, and_22_out, and_23_out, and_24_out, and_25_out,
       and_26_out, and_27_out, and_28_out, and_29_out, and_30_out, Clock, Not_In0, Not_In1, Not_Q0, Not_Q1,
       Not_Q2, or_1_out, or_2_out, or_3_out, Q0, Q1, Q2;

  not not_1 (Not_In1, In1);
  not not_2 (Not_In0, In0);
  and and_1 (and_1_out, Not_Q2, Q1, Q0, Not_In1, In0);
  and and_2 (and_2_out, Not_Q2, Q1, Not_Q0, Not_In1, In0);
  and and_3 (and_3_out, Not_Q2, Q1, Q0, Not_In1, Not_In0);
  and and_4 (and_4_out, Not_Q2, Q1, Not_Q0, In1, Not_In0);
  and and_5 (and_5_out, Not_Q2, Q1, Q0, In1, Not_In0);
  and and_6 (and_6_out, Not_Q2, Not_Q1, Q0, In1, Not_In0);
  and and_7 (and_7_out, Not_Q2, Q1, Q0, In1, Not_In0);
  and and_8 (and_8_out, Not_Q2, Not_Q1, Q0, In1, Not_In0);
  and and_9 (and_9_out, Not_Q2, Q1, Q0, Not_In1, Not_In0);
  and and_10 (and_10_out, Not_Q2, Q1, Not_Q0, In1, In0);
  and and_11 (and_11_out, Q2, Not_Q1, Not_Q0, In1, Not_In0);
  and and_12 (and_12_out, Q2, Not_Q1, Q0, In1, Not_In0);
  and and_13 (and_13_out, Q2, Not_Q1, Not_Q0, Not_In1, In0);
  and and_14 (and_14_out, Q2, Not_Q1, Not_Q0, Not_In1, Not_In0);
  and and_15 (and_15_out, Not_Q2, Not_Q1, Q0, Not_In1, Not_In0);
  and and_16 (and_16_out, Q2, Not_Q1, Not_Q0, Not_In1, In0);
  and and_17 (and_17_out, Not_Q2, Not_Q1, Q0, Not_In1, In0);
  and and_18 (and_18_out, Not_Q2, Q1, Not_Q0, Not_In1, In0);
  and and_19 (and_19_out, Not_Q2, Q1, Q0, In1, In0);
  and and_20 (and_20_out, Q2, Not_Q1, Q0, Not_In1, In0);
  and and_21 (and_21_out, Not_Q2, Not_Q1, Not_Q0, In1, In0);
  and and_22 (and_22_out, Not_Q2, Not_Q1, Not_Q0, In1, In0);
  and and_23 (and_23_out, Q2, Not_Q1, Q0, Not_In1, Not_In0);
  and and_24 (and_24_out, Not_Q2, Not_Q1, Not_Q0, In1, Not_In0);
  and and_25 (and_25_out, Not_Q2, Q1, Not_Q0, Not_In1, Not_In0);
  and and_26 (and_26_out, Not_Q2, Not_Q1, Q0, In1, In0);
  and and_27 (and_27_out, Q2, Not_Q1, Not_Q0, In1, In0);
  and and_28 (and_28_out, Q2, Not_Q1, Q0, In1, In0);
  D_Flip_Flop u_Q2 (.clk(Clock), .D(or_1_out), .Q(Q2), .Qn(Not_Q2));  // open: preset, en, reset
  or or_1 (or_1_out, and_22_out, and_13_out, and_4_out, and_1_out, and_5_out, and_14_out, and_23_out);
  or or_2 (or_2_out, and_24_out, and_17_out, and_8_out, and_9_out, and_18_out, and_25_out);
  and and_29 (and_29_out, Not_Q2, Not_Q1, Not_Q0, Not_In1, In0);
  or or_3 (or_3_out, and_29_out, and_21_out, and_15_out, and_6_out, and_2_out, and_3_out, and_7_out, and_16_out, and_30_out);
  and and_30 (and_30_out, Q2, Not_Q1, Q0, Not_In1, Not_In0);
  or or_4 (out_3, and_26_out, and_10_out, and_19_out, and_11_out, and_20_out, and_27_out, and_12_out, and_28_out);
  D_Flip_Flop u_Q1 (.clk(Clock), .D(or_2_out), .Q(Q1), .Qn(Not_Q1));  // open: preset, en, reset
  D_Flip_Flop u_Q0 (.clk(Clock), .D(or_3_out), .Q(Q0), .Qn(Not_Q0));  // open: preset, en, reset
  Button button_1 (.out(Clock));

  // Notes on the sheet:
  //   N: In1 = 0, In0 =1
  //   D: In1 = 1, In0 =0
  //   Q: In1 = 1, In0 =1
  //   Input: 0 = 00, N = 01, D = 10, Q = 11
endmodule
