// Logisim project jsw50_HW3_3e.circ as structural Verilog: 1 circuit, main circuit main
module main (
  input  In3,
  input  In2,
  input  In1,
  input  In0
);

  wire _0, _1, _2, _3, _4, _5, _6, _7, _8, _9, A, b, c, d, E, F, Not_In0, Not_In1, Not_In2, Not_In3, t, u, v,
       w, x, y, z;

  not not_1 (Not_In3, In3);
  not not_2 (Not_In2, In2);
  not not_3 (Not_In1, In1);
  not not_4 (Not_In0, In0);
  or or_1 (t, _2, _3, _4, _5, _6, _8, _9, A, b, c, d, E, F);
  or or_2 (u, _0, _4, _5, _6, _8, _9, A, b, E, F);
  and and_1 (_0, Not_In3, Not_In2, Not_In1, Not_In0);
  and and_2 (_4, Not_In3, In2, Not_In1, Not_In0);
  and and_3 (_8, In3, Not_In2, Not_In1, Not_In0);
  and and_4 (c, In3, In2, Not_In1, Not_In0);
  or or_3 (v, _0, _2, _3, _5, _6, _7, _8, _9, A, E, F);
  or or_4 (w, _0, _1, _2, _3, _4, _7, _8, _9, A, d);
  and and_5 (_1, Not_In3, Not_In2, Not_In1, In0);
  and and_6 (_5, Not_In3, In2, Not_In1, In0);
  and and_7 (_9, In3, Not_In2, Not_In1, In0);
  and and_8 (d, In3, In2, Not_In1, In0);
  or or_5 (x, _0, _2, _6, _8, A, b, c, d, E, F);
  or or_6 (y, _0, _2, _3, _5, _6, _8, b, c, d, E);
  and and_9 (_2, Not_In3, Not_In2, In1, Not_In0);
  and and_10 (_6, Not_In3, In2, In1, Not_In0);
  and and_11 (A, In3, Not_In2, In1, Not_In0);
  and and_12 (E, In3, In2, In1, Not_In0);
  or or_7 (z, _0, _1, _3, _4, _5, _6, _7, _8, _9, A, b, d);
  and and_13 (_3, Not_In3, Not_In2, In1, In0);
  and and_14 (_7, Not_In3, In2, In1, In0);
  and and_15 (b, In3, Not_In2, In1, In0);
  and and_16 (F, In3, In2, In1, In0);
  _7_Segment_Display u_7_segment_display_1 (.g(t), .f(u), .a(v), .b(w), .e(x), .d(y), .c(z));  // open: dp
endmodule
