// Logisim project jsw50_hw4.circ as structural Verilog: 11 circuits, main circuit main
module main (
  output [2:0] out_1,
  output [2:0] out_2
);

  wire button_2_out, Clock, EQUALS, ifjal_1_output, LESSTHAN, multiplexer_4_out, multiplexer_5_out,
       multiplexer_8_out, multiplexer_11_out, Reset, type_1_out_2, type_2_out_2, writeen_1_out_2;
  wire [2:0] multiplexer_6_out, multiplexer_7_out, Rs, Shamt;
  wire [3:0] opcode;
  wire [5:0] IImm;
  wire [7:0] toRt;
  wire [11:0] PCAddr;
  wire [15:0] alu_2_result, Blt, Bne, IImmEx, Instruction, J, multiplexer_1_out, multiplexer_10_out,
       n16bitadder_1_output, n16bitadder_2_output, PCInc, ram_1_data, registerfile_1_p1, RSout, RTout;

  Clock clock_1 (.out(Clock));
  Multiplexer #(.select(4), .width(16), .enable("false")) multiplexer_1 (
    .in0(PCInc), .in1(PCInc), .in2(PCInc), .in3(PCInc), .in4(PCInc), .in5(PCInc), .in6(PCInc), .in7(PCInc),
    .in8(PCInc), .in9(Bne), .in10(Blt), .in11(J), .in12(RSout), .in13(J), .in14(PCInc), .in15(PCInc),
    .out(multiplexer_1_out), .sel(opcode));
  _16bitadder u_16bitadder_1 (.A(PCInc), .B(IImmEx), .Output(n16bitadder_1_output));  // open: Zero
  _16bitadder u_16bitadder_2 (.A(PCInc), .B(IImmEx), .Output(n16bitadder_2_output));  // open: Zero
  Button button_1 (.out(Reset));
  Multiplexer #(.width(16), .enable("false")) multiplexer_2 (
    .in0(n16bitadder_1_output), .in1(PCInc), .out(Bne), .sel(EQUALS));
  Multiplexer #(.width(16), .enable("false")) multiplexer_3 (
    .in0(n16bitadder_2_output), .in1(PCInc), .out(Blt), .sel(LESSTHAN));
  ROM #(.addrWidth(16), .dataWidth(16)) rom_1 (.addr({J[15:12], PCAddr}), .data(Instruction));  // open: sel
  Register_Creator PC (
    .Clear(Reset), .Clock(Clock), .Enable(1'b1), .Input(multiplexer_1_out), .out_5({J[15:12], PCAddr}));
  Instruction_Decode instruction_decode_1 (
    .Instruction(Instruction), .opcode(opcode), .Rs(Rs), .Rt(out_2), .Address(J[11:0]), .Shamt(Shamt),
    .Immediate(IImm), .Rd(out_1));
  _16bitadder u_16bitadder_3 (.A({J[15:12], PCAddr}), .B(16'h1), .Output(PCInc));  // open: Zero
  Multiplexer #(.select(4), .enable("false")) multiplexer_4 (
    .in0(1'b0), .in1(1'b0), .in2(1'b0), .in3(1'b0), .in4(1'b0), .in5(1'b0), .in6(1'b0), .in7(1'b0),
    .in8(1'b0), .in9(1'b0), .in10(1'b0), .in11(1'b0), .in12(1'b0), .in13(1'b0), .in14(1'b0), .in15(1'b1),
    .out(multiplexer_4_out), .sel(opcode));
  WriteEn writeen_1 (.Opcode(opcode), .out_2(writeen_1_out_2));
  TTY #(.rows(4)) tty_1 (.data(RSout[6:0]), .clk(Clock), .we(multiplexer_4_out), .clr(Reset));
  Multiplexer #(.enable("false")) multiplexer_5 (
    .in0(1'b1), .in1(1'b0), .out(multiplexer_5_out), .sel(writeen_1_out_2));
  Multiplexer #(.width(3), .enable("false")) multiplexer_6 (
    .in0(out_1), .in1(out_2), .out(multiplexer_6_out), .sel(type_1_out_2));
  Type type_1 (.Opcode(opcode), .out_2(type_1_out_2));
  ALU alu_1 (.A(RSout), .B(RTout), .EQUALS(EQUALS));  // open: Shamt, Operation, Result, LESS
  // Probe on multiplexer_5_out
  Multiplexer #(.width(3), .enable("false")) multiplexer_7 (
    .in0(multiplexer_6_out), .in1(3'b111), .out(multiplexer_7_out), .sel(ifjal_1_output));
  ifJal ifjal_1 (.in_1(opcode), .Output(ifjal_1_output));
  // RegisterFile registerfile_1: pin names not known; wires that end beside it: registerfile_1_p1, Clock, multiplexer_5_out, multiplexer_7_out, Rs, out_2, RSout, RTout
  Keyboard keyboard_1 (.clk(Clock), .re(multiplexer_8_out), .clr(Reset), .avail(toRt[7]), .data(toRt[6:0]));
  Multiplexer #(.select(4), .enable("false")) multiplexer_8 (
    .in0(1'b0), .in1(1'b0), .in2(1'b0), .in3(1'b0), .in4(1'b0), .in5(1'b0), .in6(1'b0), .in7(1'b0),
    .in8(1'b0), .in9(1'b0), .in10(1'b0), .in11(1'b0), .in12(1'b0), .in13(1'b0), .in14(1'b1), .in15(1'b0),
    .out(multiplexer_8_out), .sel(opcode));
  Multiplexer #(.select(4), .width(16), .enable("false")) multiplexer_9 (
    .in0(alu_2_result), .in1(alu_2_result), .in2(alu_2_result), .in3(alu_2_result), .in4(alu_2_result),
    .in5(alu_2_result), .in6(alu_2_result), .in7(ram_1_data), .in8(alu_2_result), .in9(alu_2_result),
    .in10(alu_2_result), .in11(alu_2_result), .in12(alu_2_result), .in13(PCInc), .in14({{8{1'b0}}, toRt}),
    .in15(alu_2_result), .out(registerfile_1_p1), .sel(opcode));
  Multiplexer #(.width(16), .enable("false")) multiplexer_10 (
    .in0(RTout), .in1(IImmEx), .out(multiplexer_10_out), .sel(type_2_out_2));
  Type type_2 (.Opcode(opcode), .out_2(type_2_out_2));
  SignExtend signextend_1 (.in_1(IImm), .out_2(IImmEx));
  ALU alu_2 (
    .Shamt(Shamt), .A(RSout), .B(multiplexer_10_out), .Operation(opcode), .Result(alu_2_result),
    .LESS(LESSTHAN));  // open: EQUALS
  Multiplexer #(.select(4), .enable("false")) multiplexer_11 (
    .in0(1'b0), .in1(1'b0), .in2(1'b0), .in3(1'b0), .in4(1'b0), .in5(1'b0), .in6(1'b0), .in7(1'b0),
    .in8(1'b1), .in9(1'b0), .in10(1'b0), .in11(1'b0), .in12(1'b0), .in13(1'b0), .in14(1'b0), .in15(1'b0),
    .out(multiplexer_11_out), .sel(opcode));
  RAM #(.addrWidth(16), .dataWidth(16), .bus("separate")) ram_1 (
    .addr(alu_2_result), .din(RTout), .data(ram_1_data), .str(multiplexer_11_out), .clk(Clock),
    .clr(button_2_out));  // open: sel, ld
  Button button_2 (.out(button_2_out));

  // Other names for the same wires on the sheet: JAddress[11:0] = J[11:0]; PCAddr[15:12] = J[15:12]; Rd[2:0] = out_1;
  //   Rt[2:0] = out_2

  // Notes on the sheet:
  //   Fetch
  //   contents of rom_1 (hex, n*v repeats v):
  //   1048 520d 1240 520d 1240 5209 1240 d01d e140 1048 520d 1240 520d 1243 5209 1241 7280 2558 3500 4528
  //   541a 641a 14be 6411 a401 410 91ff 1fc1 91ff 72c0 f600 1241 963c ce00
endmodule

module Opcode_Decode (
  input  [3:0] in_1,
  output add,
  output \not ,
  output jr,
  output srl,
  output addi,
  output \xor ,
  output lw,
  output jal,
  output sll,
  output \input ,
  output sub,
  output sw,
  output blt,
  output \output ,
  output bne,
  output j
);

  wire Not_In0, Not_In1, Not_In2, Not_In3;

  and and_1 (add, Not_In3, Not_In2, Not_In1, Not_In0);
  and and_2 (addi, Not_In3, Not_In2, Not_In1, in_1[0]);
  and and_3 (sub, Not_In3, Not_In2, in_1[1], Not_In0);
  and and_4 (bne, in_1[3], Not_In2, Not_In1, in_1[0]);
  not not_1 (Not_In0, in_1[0]);
  not not_2 (Not_In1, in_1[1]);
  not not_3 (Not_In2, in_1[2]);
  not not_4 (Not_In3, in_1[3]);
  and and_5 (\not , Not_In3, Not_In2, in_1[1], in_1[0]);
  and and_6 (\xor , Not_In3, in_1[2], Not_In1, Not_In0);
  and and_7 (sll, Not_In3, in_1[2], Not_In1, in_1[0]);
  and and_8 (blt, in_1[3], Not_In2, in_1[1], Not_In0);
  and and_9 (srl, Not_In3, in_1[2], in_1[1], Not_In0);
  and and_10 (lw, Not_In3, in_1[2], in_1[1], in_1[0]);
  and and_11 (sw, in_1[3], Not_In2, Not_In1, Not_In0);
  and and_12 (j, in_1[3], Not_In2, in_1[1], in_1[0]);
  and and_13 (jr, in_1[3], in_1[2], Not_In1, Not_In0);
  and and_14 (jal, in_1[3], in_1[2], Not_In1, in_1[0]);
  and and_15 (\input , in_1[3], in_1[2], in_1[1], Not_In0);
  and and_16 (\output , in_1[3], in_1[2], in_1[1], in_1[0]);

  // Other names for the same wires on the sheet: In0 = in_1[0]; In1 = in_1[1]; In2 = in_1[2]; In3 = in_1[3]
endmodule

// InstDec
module Instruction_Decode (
  input  [15:0] Instruction,
  output [11:0] Address,
  output [2:0] Shamt,
  output [5:0] Immediate,
  output [2:0] Rd,
  output [2:0] Rt,
  output [2:0] Rs,
  output [3:0] opcode
);


  assign Address = Instruction[11:0];
  assign Immediate = Instruction[5:0];
  assign opcode = Instruction[15:12];
  assign Rd = Instruction[5:3];
  assign Rs = Instruction[11:9];
  assign Rt = Instruction[8:6];
  assign Shamt = Instruction[2:0];
endmodule

module ALU (
  input  [2:0] Shamt,
  input  [15:0] A,
  input  [15:0] B,
  input  [3:0] Operation,
  output [15:0] Result,
  output LESS,
  output EQUALS
);

  wire Add0, Add1, Add2, Add3, Add4, Add5, Add6, Add7, Add8, Add9, Add10, Add11, Add12, Add13, Add14, Add15,
       and_1_out, and_3_out, multiplexer_3_out, multiplexer_4_out, multiplexer_5_out, multiplexer_6_out,
       multiplexer_7_out, multiplexer_8_out, multiplexer_9_out, multiplexer_10_out, multiplexer_12_out,
       multiplexer_13_out, multiplexer_14_out, multiplexer_15_out, multiplexer_16_out, multiplexer_17_out,
       multiplexer_18_out, multiplexer_19_out, multiplexer_20_out, multiplexer_21_out, multiplexer_22_out,
       multiplexer_23_out, multiplexer_24_out, multiplexer_25_out, multiplexer_26_out, multiplexer_27_out,
       multiplexer_28_out, multiplexer_29_out, multiplexer_30_out, multiplexer_31_out, multiplexer_32_out,
       multiplexer_33_out, multiplexer_34_out, multiplexer_35_out, multiplexer_36_out, multiplexer_37_out,
       multiplexer_38_out, multiplexer_39_out, multiplexer_40_out, multiplexer_41_out, multiplexer_42_out,
       multiplexer_43_out, multiplexer_44_out, multiplexer_45_out, multiplexer_46_out, multiplexer_47_out,
       multiplexer_48_out, multiplexer_49_out, multiplexer_50_out, multiplexer_51_out, multiplexer_52_out,
       multiplexer_53_out, multiplexer_55_out, multiplexer_56_out, multiplexer_57_out, multiplexer_58_out,
       multiplexer_60_out, multiplexer_61_out, multiplexer_62_out, multiplexer_65_out, multiplexer_66_out,
       multiplexer_68_out, multiplexer_71_out, multiplexer_72_out, multiplexer_75_out, multiplexer_76_out,
       n1bitadder_1_carryout, n1bitadder_2_carryout, n1bitadder_3_carryout, n1bitadder_4_carryout,
       n1bitadder_5_carryout, n1bitadder_6_carryout, n1bitadder_7_carryout, n1bitadder_8_carryout,
       n1bitadder_9_carryout, n1bitadder_10_carryout, n1bitadder_11_carryout, n1bitadder_12_carryout,
       n1bitadder_13_carryout, n1bitadder_14_carryout, n1bitadder_15_carryout, n1bitadder_17_carryout,
       n1bitadder_18_carryout, n1bitadder_19_carryout, n1bitadder_20_carryout, n1bitadder_21_carryout,
       n1bitadder_22_carryout, n1bitadder_23_carryout, n1bitadder_24_carryout, n1bitadder_25_carryout,
       n1bitadder_26_carryout, n1bitadder_27_carryout, n1bitadder_28_carryout, n1bitadder_29_carryout,
       n1bitadder_30_carryout, n1bitadder_31_carryout, not_3_out, not_4_out, not_5_out, not_6_out, not_7_out,
       not_8_out, not_9_out, not_10_out, not_11_out, not_12_out, not_13_out, not_14_out, not_15_out,
       not_16_out, not_17_out, not_18_out, Sub0, Sub1, Sub2, Sub3, Sub4, Sub5, Sub6, Sub7, Sub8, Sub9, Sub10,
       Sub11, Sub12, Sub13, Sub14, Sub15, xnor_1_out, xnor_2_out, xnor_3_out, xnor_4_out, xnor_5_out,
       xnor_6_out, xnor_7_out, xnor_8_out, xnor_9_out, xnor_10_out, xnor_11_out, xnor_12_out, xnor_13_out,
       xnor_14_out, xnor_15_out, xnor_16_out;
  wire [15:0] ANot, LESSTHAN, SHIFTLEFT, SHIFTRIGHT, XOR, ZERO;

  _1bitadder u_1bitadder_1 (.A(A[0]), .B(B[0]), .Carry_In(1'b0), .Add(Add0), .CarryOut(n1bitadder_1_carryout));
  _1bitadder u_1bitadder_2 (
    .A(A[1]), .B(B[1]), .Carry_In(n1bitadder_1_carryout), .Add(Add1), .CarryOut(n1bitadder_2_carryout));
  _1bitadder u_1bitadder_3 (
    .A(A[2]), .B(B[2]), .Carry_In(n1bitadder_2_carryout), .Add(Add2), .CarryOut(n1bitadder_3_carryout));
  _1bitadder u_1bitadder_4 (
    .A(A[3]), .B(B[3]), .Carry_In(n1bitadder_3_carryout), .Add(Add3), .CarryOut(n1bitadder_4_carryout));
  _1bitadder u_1bitadder_5 (
    .A(A[4]), .B(B[4]), .Carry_In(n1bitadder_4_carryout), .Add(Add4), .CarryOut(n1bitadder_5_carryout));
  _1bitadder u_1bitadder_6 (
    .A(A[5]), .B(B[5]), .Carry_In(n1bitadder_5_carryout), .Add(Add5), .CarryOut(n1bitadder_6_carryout));
  _1bitadder u_1bitadder_7 (
    .A(A[6]), .B(B[6]), .Carry_In(n1bitadder_6_carryout), .Add(Add6), .CarryOut(n1bitadder_7_carryout));
  _1bitadder u_1bitadder_8 (
    .A(A[7]), .B(B[7]), .Carry_In(n1bitadder_7_carryout), .Add(Add7), .CarryOut(n1bitadder_8_carryout));
  _1bitadder u_1bitadder_9 (
    .A(A[8]), .B(B[8]), .Carry_In(n1bitadder_8_carryout), .Add(Add8), .CarryOut(n1bitadder_9_carryout));
  _1bitadder u_1bitadder_10 (
    .A(A[9]), .B(B[9]), .Carry_In(n1bitadder_9_carryout), .Add(Add9), .CarryOut(n1bitadder_10_carryout));
  _1bitadder u_1bitadder_11 (
    .A(A[10]), .B(B[10]), .Carry_In(n1bitadder_10_carryout), .Add(Add10), .CarryOut(n1bitadder_11_carryout));
  _1bitadder u_1bitadder_12 (
    .A(A[11]), .B(B[11]), .Carry_In(n1bitadder_11_carryout), .Add(Add11), .CarryOut(n1bitadder_12_carryout));
  _1bitadder u_1bitadder_13 (
    .A(A[12]), .B(B[12]), .Carry_In(n1bitadder_12_carryout), .Add(Add12), .CarryOut(n1bitadder_13_carryout));
  _1bitadder u_1bitadder_14 (
    .A(A[13]), .B(B[13]), .Carry_In(n1bitadder_13_carryout), .Add(Add13), .CarryOut(n1bitadder_14_carryout));
  _1bitadder u_1bitadder_15 (
    .A(A[14]), .B(B[14]), .Carry_In(n1bitadder_14_carryout), .Add(Add14), .CarryOut(n1bitadder_15_carryout));
  _1bitadder u_1bitadder_16 (.A(A[15]), .B(B[15]), .Carry_In(n1bitadder_15_carryout), .Add(Add15));  // open: CarryOut
  and and_1 (and_1_out, Sub15, 1'b1);
  xnor xnor_1 (xnor_1_out, A[0], B[0]);
  xnor xnor_2 (xnor_2_out, A[1], B[1]);
  xnor xnor_3 (xnor_3_out, A[2], B[2]);
  xnor xnor_4 (xnor_4_out, A[3], B[3]);
  xnor xnor_5 (xnor_5_out, A[4], B[4]);
  xnor xnor_6 (xnor_6_out, A[5], B[5]);
  xnor xnor_7 (xnor_7_out, A[6], B[6]);
  xnor xnor_8 (xnor_8_out, A[7], B[7]);
  xnor xnor_9 (xnor_9_out, A[8], B[8]);
  xnor xnor_10 (xnor_10_out, A[9], B[9]);
  xnor xnor_11 (xnor_11_out, A[10], B[10]);
  xnor xnor_12 (xnor_12_out, A[11], B[11]);
  xnor xnor_13 (xnor_13_out, A[12], B[12]);
  xnor xnor_14 (xnor_14_out, A[13], B[13]);
  xnor xnor_15 (xnor_15_out, A[14], B[14]);
  xnor xnor_16 (xnor_16_out, A[15], B[15]);
  Multiplexer #(.width(16), .enable("false")) multiplexer_1 (.in0(B), .in1(A), .out(LESSTHAN), .sel(and_1_out));
  and and_2 (EQUALS, xnor_1_out, xnor_2_out, xnor_3_out, xnor_4_out, xnor_5_out, xnor_6_out, xnor_7_out, xnor_8_out, xnor_9_out, xnor_10_out, xnor_11_out, xnor_12_out, xnor_13_out, xnor_14_out, xnor_15_out, xnor_16_out);
  assign ANot = ~A;  // NOT_Gate not_1, 16 bits wide
  and and_3 (and_3_out, Sub15, 1'b1);
  Multiplexer #(.enable("false")) multiplexer_2 (.in0(1'b0), .in1(1'b1), .out(LESS), .sel(and_3_out));
  assign XOR = A ^ B;  // XOR_Gate xor_1, 16 bits wide
  assign ZERO = ~{Add15, Add14, Add13, Add12, Add11, Add10, Add9, Add7, Add8, Add6, Add5, Add4, Add3, Add2, Add1, Add0};  // NOT_Gate not_2, 16 bits wide
  not not_3 (not_3_out, B[0]);
  not not_4 (not_4_out, B[1]);
  not not_5 (not_5_out, B[2]);
  not not_6 (not_6_out, B[3]);
  not not_7 (not_7_out, B[4]);
  not not_8 (not_8_out, B[5]);
  not not_9 (not_9_out, B[6]);
  not not_10 (not_10_out, B[7]);
  not not_11 (not_11_out, B[8]);
  not not_12 (not_12_out, B[9]);
  not not_13 (not_13_out, B[10]);
  not not_14 (not_14_out, B[11]);
  not not_15 (not_15_out, B[12]);
  not not_16 (not_16_out, B[13]);
  not not_17 (not_17_out, B[14]);
  not not_18 (not_18_out, B[15]);
  _1bitadder u_1bitadder_17 (.A(A[0]), .B(not_3_out), .Carry_In(1'b1), .Add(Sub0), .CarryOut(n1bitadder_17_carryout));
  _1bitadder u_1bitadder_18 (
    .A(A[1]), .B(not_4_out), .Carry_In(n1bitadder_17_carryout), .Add(Sub1), .CarryOut(n1bitadder_18_carryout));
  _1bitadder u_1bitadder_19 (
    .A(A[2]), .B(not_5_out), .Carry_In(n1bitadder_18_carryout), .Add(Sub2), .CarryOut(n1bitadder_19_carryout));
  _1bitadder u_1bitadder_20 (
    .A(A[3]), .B(not_6_out), .Carry_In(n1bitadder_19_carryout), .Add(Sub3), .CarryOut(n1bitadder_20_carryout));
  _1bitadder u_1bitadder_21 (
    .A(A[4]), .B(not_7_out), .Carry_In(n1bitadder_20_carryout), .Add(Sub4), .CarryOut(n1bitadder_21_carryout));
  _1bitadder u_1bitadder_22 (
    .A(A[5]), .B(not_8_out), .Carry_In(n1bitadder_21_carryout), .Add(Sub5), .CarryOut(n1bitadder_22_carryout));
  _1bitadder u_1bitadder_23 (
    .A(A[6]), .B(not_9_out), .Carry_In(n1bitadder_22_carryout), .Add(Sub6), .CarryOut(n1bitadder_23_carryout));
  _1bitadder u_1bitadder_24 (
    .A(A[7]), .B(not_10_out), .Carry_In(n1bitadder_23_carryout), .Add(Sub7), .CarryOut(n1bitadder_24_carryout));
  _1bitadder u_1bitadder_25 (
    .A(A[8]), .B(not_11_out), .Carry_In(n1bitadder_24_carryout), .Add(Sub8), .CarryOut(n1bitadder_25_carryout));
  _1bitadder u_1bitadder_26 (
    .A(A[9]), .B(not_12_out), .Carry_In(n1bitadder_25_carryout), .Add(Sub9), .CarryOut(n1bitadder_26_carryout));
  _1bitadder u_1bitadder_27 (
    .A(A[10]), .B(not_13_out), .Carry_In(n1bitadder_26_carryout), .Add(Sub10),
    .CarryOut(n1bitadder_27_carryout));
  _1bitadder u_1bitadder_28 (
    .A(A[11]), .B(not_14_out), .Carry_In(n1bitadder_27_carryout), .Add(Sub11),
    .CarryOut(n1bitadder_28_carryout));
  _1bitadder u_1bitadder_29 (
    .A(A[12]), .B(not_15_out), .Carry_In(n1bitadder_28_carryout), .Add(Sub12),
    .CarryOut(n1bitadder_29_carryout));
  _1bitadder u_1bitadder_30 (
    .A(A[13]), .B(not_16_out), .Carry_In(n1bitadder_29_carryout), .Add(Sub13),
    .CarryOut(n1bitadder_30_carryout));
  _1bitadder u_1bitadder_31 (
    .A(A[14]), .B(not_17_out), .Carry_In(n1bitadder_30_carryout), .Add(Sub14),
    .CarryOut(n1bitadder_31_carryout));
  _1bitadder u_1bitadder_32 (
    .A(A[15]), .B(not_18_out), .Carry_In(n1bitadder_31_carryout), .Add(Sub15));  // open: CarryOut
  Multiplexer #(.enable("false")) multiplexer_3 (.in0(A[15]), .in1(A[14]), .out(multiplexer_3_out), .sel(Shamt[0]));
  Multiplexer #(.enable("false")) multiplexer_4 (.in0(A[14]), .in1(A[13]), .out(multiplexer_4_out), .sel(Shamt[0]));
  Multiplexer #(.enable("false")) multiplexer_5 (.in0(A[13]), .in1(A[12]), .out(multiplexer_5_out), .sel(Shamt[0]));
  Multiplexer #(.enable("false")) multiplexer_6 (.in0(A[12]), .in1(A[11]), .out(multiplexer_6_out), .sel(Shamt[0]));
  Multiplexer #(.enable("false")) multiplexer_7 (
    .in0(multiplexer_3_out), .in1(multiplexer_5_out), .out(multiplexer_7_out), .sel(Shamt[1]));
  Multiplexer #(.enable("false")) multiplexer_8 (.in0(A[11]), .in1(A[10]), .out(multiplexer_8_out), .sel(Shamt[0]));
  Multiplexer #(.enable("false")) multiplexer_9 (.in0(A[10]), .in1(A[9]), .out(multiplexer_9_out), .sel(Shamt[0]));
  Multiplexer #(.enable("false")) multiplexer_10 (.in0(A[9]), .in1(A[8]), .out(multiplexer_10_out), .sel(Shamt[0]));
  Multiplexer #(.select(4), .width(16), .enable("false")) multiplexer_11 (
    .in0({Add15, Add14, Add13, Add12, Add11, Add10, Add9, Add8, Add7, Add6, Add5, Add4, Add3, Add2, Add1, Add0}),
    .in1({Add15, Add14, Add13, Add12, Add11, Add10, Add9, Add8, Add7, Add6, Add5, Add4, Add3, Add2, Add1, Add0}),
    .in2({Sub15, Sub14, Sub13, Sub12, Sub11, Sub10, Sub9, Sub8, Sub7, Sub6, Sub5, Sub4, Sub3, Sub2, Sub1, Sub0}),
    .in3(ANot), .in4(XOR), .in5(SHIFTLEFT), .in6(SHIFTRIGHT),
    .in7({Add15, Add14, Add13, Add12, Add11, Add10, Add9, Add8, Add7, Add6, Add5, Add4, Add3, Add2, Add1, Add0}),
    .in8({Add15, Add14, Add13, Add12, Add11, Add10, Add9, Add8, Add7, Add6, Add5, Add4, Add3, Add2, Add1, Add0}),
    .in9({Sub15, Sub14, Sub13, Sub12, Sub11, Sub10, Sub9, Sub8, Sub7, Sub6, Sub5, Sub4, Sub3, Sub2, Sub1, Sub0}),
    .in10(LESSTHAN), .in11(A), .in12(A),
    .in13({Add15, Add14, Add13, Add12, Add11, Add10, Add9, Add8, Add7, Add6, Add5, Add4, Add3, Add2, Add1, Add0}),
    .in14(A), .in15(A), .out(Result), .sel(Operation));
  Multiplexer #(.enable("false")) multiplexer_12 (.in0(A[8]), .in1(A[7]), .out(multiplexer_12_out), .sel(Shamt[0]));
  Multiplexer #(.enable("false")) multiplexer_13 (.in0(A[7]), .in1(A[6]), .out(multiplexer_13_out), .sel(Shamt[0]));
  Multiplexer #(.enable("false")) multiplexer_14 (
    .in0(multiplexer_4_out), .in1(multiplexer_6_out), .out(multiplexer_14_out), .sel(Shamt[1]));
  Multiplexer #(.enable("false")) multiplexer_15 (
    .in0(multiplexer_5_out), .in1(multiplexer_8_out), .out(multiplexer_15_out), .sel(Shamt[1]));
  Multiplexer #(.enable("false")) multiplexer_16 (.in0(A[6]), .in1(A[5]), .out(multiplexer_16_out), .sel(Shamt[0]));
  Multiplexer #(.enable("false")) multiplexer_17 (
    .in0(multiplexer_6_out), .in1(multiplexer_9_out), .out(multiplexer_17_out), .sel(Shamt[1]));
  Multiplexer #(.enable("false")) multiplexer_18 (
    .in0(multiplexer_8_out), .in1(multiplexer_10_out), .out(multiplexer_18_out), .sel(Shamt[1]));
  Multiplexer #(.enable("false")) multiplexer_19 (.in0(A[5]), .in1(A[4]), .out(multiplexer_19_out), .sel(Shamt[0]));
  Multiplexer #(.enable("false")) multiplexer_20 (.in0(A[4]), .in1(A[3]), .out(multiplexer_20_out), .sel(Shamt[0]));
  Multiplexer #(.enable("false")) multiplexer_21 (.in0(A[0]), .in1(A[1]), .out(multiplexer_21_out), .sel(Shamt[0]));
  Multiplexer #(.enable("false")) multiplexer_22 (
    .in0(multiplexer_9_out), .in1(multiplexer_12_out), .out(multiplexer_22_out), .sel(Shamt[1]));
  Multiplexer #(.enable("false")) multiplexer_23 (
    .in0(multiplexer_12_out), .in1(multiplexer_16_out), .out(multiplexer_23_out), .sel(Shamt[1]));
  Multiplexer #(.enable("false")) multiplexer_24 (.in0(A[3]), .in1(A[2]), .out(multiplexer_24_out), .sel(Shamt[0]));
  Multiplexer #(.enable("false")) multiplexer_25 (.in0(A[2]), .in1(A[1]), .out(multiplexer_25_out), .sel(Shamt[0]));
  Multiplexer #(.enable("false")) multiplexer_26 (.in0(A[1]), .in1(A[2]), .out(multiplexer_26_out), .sel(Shamt[0]));
  Multiplexer #(.enable("false")) multiplexer_27 (.in0(A[2]), .in1(A[3]), .out(multiplexer_27_out), .sel(Shamt[0]));
  Multiplexer #(.enable("false")) multiplexer_28 (
    .in0(multiplexer_10_out), .in1(multiplexer_13_out), .out(multiplexer_28_out), .sel(Shamt[1]));
  Multiplexer #(.enable("false")) multiplexer_29 (
    .in0(multiplexer_13_out), .in1(multiplexer_19_out), .out(multiplexer_29_out), .sel(Shamt[1]));
  Multiplexer #(.enable("false")) multiplexer_30 (.in0(A[1]), .in1(A[0]), .out(multiplexer_30_out), .sel(Shamt[0]));
  Multiplexer #(.enable("false")) multiplexer_31 (.in0(A[0]), .in1(1'b0), .out(multiplexer_31_out), .sel(Shamt[0]));
  Multiplexer #(.enable("false")) multiplexer_32 (.in0(A[3]), .in1(A[4]), .out(multiplexer_32_out), .sel(Shamt[0]));
  Multiplexer #(.enable("false")) multiplexer_33 (
    .in0(multiplexer_16_out), .in1(multiplexer_20_out), .out(multiplexer_33_out), .sel(Shamt[1]));
  Multiplexer #(.enable("false")) multiplexer_34 (
    .in0(multiplexer_21_out), .in1(multiplexer_27_out), .out(multiplexer_34_out), .sel(Shamt[1]));
  Multiplexer #(.enable("false")) multiplexer_35 (.in0(A[4]), .in1(A[5]), .out(multiplexer_35_out), .sel(Shamt[0]));
  Multiplexer #(.enable("false")) multiplexer_36 (.in0(A[5]), .in1(A[6]), .out(multiplexer_36_out), .sel(Shamt[0]));
  Multiplexer #(.enable("false")) multiplexer_37 (
    .in0(multiplexer_19_out), .in1(multiplexer_24_out), .out(multiplexer_37_out), .sel(Shamt[1]));
  Multiplexer #(.enable("false")) multiplexer_38 (
    .in0(multiplexer_20_out), .in1(multiplexer_25_out), .out(multiplexer_38_out), .sel(Shamt[1]));
  Multiplexer #(.enable("false")) multiplexer_39 (.in0(A[6]), .in1(A[7]), .out(multiplexer_39_out), .sel(Shamt[0]));
  Multiplexer #(.enable("false")) multiplexer_40 (.in0(A[7]), .in1(A[8]), .out(multiplexer_40_out), .sel(Shamt[0]));
  Multiplexer #(.enable("false")) multiplexer_41 (
    .in0(multiplexer_24_out), .in1(multiplexer_30_out), .out(multiplexer_41_out), .sel(Shamt[1]));
  Multiplexer #(.enable("false")) multiplexer_42 (
    .in0(multiplexer_25_out), .in1(multiplexer_31_out), .out(multiplexer_42_out), .sel(Shamt[1]));
  Multiplexer #(.enable("false")) multiplexer_43 (.in0(A[8]), .in1(A[9]), .out(multiplexer_43_out), .sel(Shamt[0]));
  Multiplexer #(.enable("false")) multiplexer_44 (
    .in0(multiplexer_30_out), .in1(1'b0), .out(multiplexer_44_out), .sel(Shamt[1]));
  Multiplexer #(.enable("false")) multiplexer_45 (
    .in0(multiplexer_26_out), .in1(multiplexer_32_out), .out(multiplexer_45_out), .sel(Shamt[1]));
  Multiplexer #(.enable("false")) multiplexer_46 (
    .in0(multiplexer_27_out), .in1(multiplexer_35_out), .out(multiplexer_46_out), .sel(Shamt[1]));
  Multiplexer #(.enable("false")) multiplexer_47 (
    .in0(multiplexer_32_out), .in1(multiplexer_36_out), .out(multiplexer_47_out), .sel(Shamt[1]));
  Multiplexer #(.enable("false")) multiplexer_48 (.in0(A[9]), .in1(A[10]), .out(multiplexer_48_out), .sel(Shamt[0]));
  Multiplexer #(.enable("false")) multiplexer_49 (
    .in0(multiplexer_31_out), .in1(1'b0), .out(multiplexer_49_out), .sel(Shamt[1]));
  Multiplexer #(.enable("false")) multiplexer_50 (
    .in0(multiplexer_35_out), .in1(multiplexer_39_out), .out(multiplexer_50_out), .sel(Shamt[1]));
  Multiplexer #(.enable("false")) multiplexer_51 (.in0(A[10]), .in1(A[11]), .out(multiplexer_51_out), .sel(Shamt[0]));
  Multiplexer #(.enable("false")) multiplexer_52 (.in0(A[11]), .in1(A[12]), .out(multiplexer_52_out), .sel(Shamt[0]));
  Multiplexer #(.enable("false")) multiplexer_53 (.in0(A[12]), .in1(A[13]), .out(multiplexer_53_out), .sel(Shamt[0]));
  Multiplexer #(.enable("false")) multiplexer_54 (
    .in0(multiplexer_7_out), .in1(multiplexer_18_out), .out(SHIFTLEFT[15]), .sel(Shamt[2]));
  Multiplexer #(.enable("false")) multiplexer_55 (
    .in0(multiplexer_36_out), .in1(multiplexer_40_out), .out(multiplexer_55_out), .sel(Shamt[1]));
  Multiplexer #(.enable("false")) multiplexer_56 (
    .in0(multiplexer_40_out), .in1(multiplexer_48_out), .out(multiplexer_56_out), .sel(Shamt[1]));
  Multiplexer #(.enable("false")) multiplexer_57 (.in0(A[13]), .in1(A[14]), .out(multiplexer_57_out), .sel(Shamt[0]));
  Multiplexer #(.enable("false")) multiplexer_58 (.in0(A[14]), .in1(A[15]), .out(multiplexer_58_out), .sel(Shamt[0]));
  Multiplexer #(.enable("false")) multiplexer_59 (
    .in0(multiplexer_14_out), .in1(multiplexer_22_out), .out(SHIFTLEFT[14]), .sel(Shamt[2]));
  Multiplexer #(.enable("false")) multiplexer_60 (
    .in0(multiplexer_39_out), .in1(multiplexer_43_out), .out(multiplexer_60_out), .sel(Shamt[1]));
  Multiplexer #(.enable("false")) multiplexer_61 (
    .in0(multiplexer_43_out), .in1(multiplexer_51_out), .out(multiplexer_61_out), .sel(Shamt[1]));
  Multiplexer #(.enable("false")) multiplexer_62 (.in0(A[15]), .in1(1'b0), .out(multiplexer_62_out), .sel(Shamt[0]));
  Multiplexer #(.enable("false")) multiplexer_63 (
    .in0(multiplexer_15_out), .in1(multiplexer_28_out), .out(SHIFTLEFT[13]), .sel(Shamt[2]));
  Multiplexer #(.enable("false")) multiplexer_64 (
    .in0(multiplexer_17_out), .in1(multiplexer_23_out), .out(SHIFTLEFT[12]), .sel(Shamt[2]));
  Multiplexer #(.enable("false")) multiplexer_65 (
    .in0(multiplexer_48_out), .in1(multiplexer_52_out), .out(multiplexer_65_out), .sel(Shamt[1]));
  Multiplexer #(.enable("false")) multiplexer_66 (
    .in0(multiplexer_51_out), .in1(multiplexer_53_out), .out(multiplexer_66_out), .sel(Shamt[1]));
  Multiplexer #(.enable("false")) multiplexer_67 (
    .in0(multiplexer_18_out), .in1(multiplexer_29_out), .out(SHIFTLEFT[11]), .sel(Shamt[2]));
  Multiplexer #(.enable("false")) multiplexer_68 (
    .in0(multiplexer_52_out), .in1(multiplexer_57_out), .out(multiplexer_68_out), .sel(Shamt[1]));
  Multiplexer #(.enable("false")) multiplexer_69 (
    .in0(multiplexer_22_out), .in1(multiplexer_33_out), .out(SHIFTLEFT[10]), .sel(Shamt[2]));
  Multiplexer #(.enable("false")) multiplexer_70 (
    .in0(multiplexer_28_out), .in1(multiplexer_37_out), .out(SHIFTLEFT[9]), .sel(Shamt[2]));
  Multiplexer #(.enable("false")) multiplexer_71 (
    .in0(multiplexer_53_out), .in1(multiplexer_58_out), .out(multiplexer_71_out), .sel(Shamt[1]));
  Multiplexer #(.enable("false")) multiplexer_72 (
    .in0(multiplexer_57_out), .in1(multiplexer_62_out), .out(multiplexer_72_out), .sel(Shamt[1]));
  Multiplexer #(.enable("false")) multiplexer_73 (
    .in0(multiplexer_23_out), .in1(multiplexer_38_out), .out(SHIFTLEFT[8]), .sel(Shamt[2]));
  Multiplexer #(.enable("false")) multiplexer_74 (
    .in0(multiplexer_29_out), .in1(multiplexer_41_out), .out(SHIFTLEFT[7]), .sel(Shamt[2]));
  Multiplexer #(.enable("false")) multiplexer_75 (
    .in0(multiplexer_58_out), .in1(1'b0), .out(multiplexer_75_out), .sel(Shamt[1]));
  Multiplexer #(.enable("false")) multiplexer_76 (
    .in0(multiplexer_62_out), .in1(1'b0), .out(multiplexer_76_out), .sel(Shamt[1]));
  Multiplexer #(.enable("false")) multiplexer_77 (
    .in0(multiplexer_33_out), .in1(multiplexer_42_out), .out(SHIFTLEFT[6]), .sel(Shamt[2]));
  Multiplexer #(.enable("false")) multiplexer_78 (
    .in0(multiplexer_37_out), .in1(multiplexer_44_out), .out(SHIFTLEFT[5]), .sel(Shamt[2]));
  Multiplexer #(.enable("false")) multiplexer_79 (
    .in0(multiplexer_38_out), .in1(multiplexer_49_out), .out(SHIFTLEFT[4]), .sel(Shamt[2]));
  Multiplexer #(.enable("false")) multiplexer_80 (
    .in0(multiplexer_34_out), .in1(multiplexer_50_out), .out(SHIFTRIGHT[0]), .sel(Shamt[2]));
  Multiplexer #(.enable("false")) multiplexer_81 (
    .in0(multiplexer_41_out), .in1(1'b0), .out(SHIFTLEFT[3]), .sel(Shamt[2]));
  Multiplexer #(.enable("false")) multiplexer_82 (
    .in0(multiplexer_45_out), .in1(multiplexer_55_out), .out(SHIFTRIGHT[1]), .sel(Shamt[2]));
  Multiplexer #(.enable("false")) multiplexer_83 (
    .in0(multiplexer_42_out), .in1(1'b0), .out(SHIFTLEFT[2]), .sel(Shamt[2]));
  Multiplexer #(.enable("false")) multiplexer_84 (
    .in0(multiplexer_44_out), .in1(1'b0), .out(SHIFTLEFT[1]), .sel(Shamt[2]));
  Multiplexer #(.enable("false")) multiplexer_85 (
    .in0(multiplexer_46_out), .in1(multiplexer_60_out), .out(SHIFTRIGHT[2]), .sel(Shamt[2]));
  Multiplexer #(.enable("false")) multiplexer_86 (
    .in0(multiplexer_47_out), .in1(multiplexer_56_out), .out(SHIFTRIGHT[3]), .sel(Shamt[2]));
  Multiplexer #(.enable("false")) multiplexer_87 (
    .in0(multiplexer_49_out), .in1(1'b0), .out(SHIFTLEFT[0]), .sel(Shamt[2]));
  Multiplexer #(.enable("false")) multiplexer_88 (
    .in0(multiplexer_50_out), .in1(multiplexer_61_out), .out(SHIFTRIGHT[4]), .sel(Shamt[2]));
  Multiplexer #(.enable("false")) multiplexer_89 (
    .in0(multiplexer_55_out), .in1(multiplexer_65_out), .out(SHIFTRIGHT[5]), .sel(Shamt[2]));
  Multiplexer #(.enable("false")) multiplexer_90 (
    .in0(multiplexer_60_out), .in1(multiplexer_66_out), .out(SHIFTRIGHT[6]), .sel(Shamt[2]));
  Multiplexer #(.enable("false")) multiplexer_91 (
    .in0(multiplexer_56_out), .in1(multiplexer_68_out), .out(SHIFTRIGHT[7]), .sel(Shamt[2]));
  Multiplexer #(.enable("false")) multiplexer_92 (
    .in0(multiplexer_61_out), .in1(multiplexer_71_out), .out(SHIFTRIGHT[8]), .sel(Shamt[2]));
  Multiplexer #(.enable("false")) multiplexer_93 (
    .in0(multiplexer_65_out), .in1(multiplexer_72_out), .out(SHIFTRIGHT[9]), .sel(Shamt[2]));
  Multiplexer #(.enable("false")) multiplexer_94 (
    .in0(multiplexer_66_out), .in1(multiplexer_75_out), .out(SHIFTRIGHT[10]), .sel(Shamt[2]));
  Multiplexer #(.enable("false")) multiplexer_95 (
    .in0(multiplexer_68_out), .in1(multiplexer_76_out), .out(SHIFTRIGHT[11]), .sel(Shamt[2]));
  Multiplexer #(.enable("false")) multiplexer_96 (
    .in0(multiplexer_71_out), .in1(1'b0), .out(SHIFTRIGHT[12]), .sel(Shamt[2]));
  Multiplexer #(.enable("false")) multiplexer_97 (
    .in0(multiplexer_72_out), .in1(1'b0), .out(SHIFTRIGHT[13]), .sel(Shamt[2]));
  Multiplexer #(.enable("false")) multiplexer_98 (
    .in0(multiplexer_75_out), .in1(1'b0), .out(SHIFTRIGHT[14]), .sel(Shamt[2]));
  Multiplexer #(.enable("false")) multiplexer_99 (
    .in0(multiplexer_76_out), .in1(1'b0), .out(SHIFTRIGHT[15]), .sel(Shamt[2]));

  // Other names for the same wires on the sheet: ADDTun[15:0] = {Add15, Add14, Add13, Add12, Add11, Add10, Add9, Add8, Add7, Add6, Add5, Add4, Add3, Add2, Add1, Add0};
  //   Atun[15:0] = A; Btun[15:0] = B; ShiftL = Shamt[0]; ShiftM = Shamt[1]; ShiftR = Shamt[2];
  //   SUBTun[15:0] = {Sub15, Sub14, Sub13, Sub12, Sub11, Sub10, Sub9, Sub8, Sub7, Sub6, Sub5, Sub4, Sub3, Sub2, Sub1, Sub0}

  // Notes on the sheet:
  //   Inputs
  //   Adder
  //   EQUALS BIT
  //   NOT
  //   LESS THAN BIT
  //   XOR
  //   Shamt input
  //   SUBTRACTOR
  //   LEFT SHIFT
  //   MULTIPLEXER
  //   RIGHT SHIFT
endmodule

module _1bitadder (
  input  A,
  input  B,
  input  Carry_In,
  output Add,
  output CarryOut
);

  wire and_1_out, and_2_out, xor_1_out;

  xor xor_1 (xor_1_out, A, B);
  and and_1 (and_1_out, Carry_In, xor_1_out);
  and and_2 (and_2_out, B, A);
  xor xor_2 (Add, xor_1_out, Carry_In);
  or or_1 (CarryOut, and_1_out, and_2_out);
endmodule

module Register_Creator (
  input  Clear,
  input  Clock,
  input  Enable,
  input  [15:0] Input,
  output [15:0] out_5
);

  D_Flip_Flop d_ff_1 (.clk(Clock), .D(Input[0]), .Q(out_5[0]), .en(Enable), .reset(Clear));  // open: Qn, preset
  D_Flip_Flop d_ff_2 (.clk(Clock), .D(Input[1]), .Q(out_5[1]), .en(Enable), .reset(Clear));  // open: Qn, preset
  D_Flip_Flop d_ff_3 (.clk(Clock), .D(Input[2]), .Q(out_5[2]), .en(Enable), .reset(Clear));  // open: Qn, preset
  D_Flip_Flop d_ff_4 (.clk(Clock), .D(Input[3]), .Q(out_5[3]), .en(Enable), .reset(Clear));  // open: Qn, preset
  D_Flip_Flop d_ff_5 (.clk(Clock), .D(Input[4]), .Q(out_5[4]), .en(Enable), .reset(Clear));  // open: Qn, preset
  // XNOR_Gate xnor_1 is placed but not wired
  // XNOR_Gate xnor_2 is placed but not wired
  D_Flip_Flop d_ff_6 (.clk(Clock), .D(Input[5]), .Q(out_5[5]), .en(Enable), .reset(Clear));  // open: Qn, preset
  D_Flip_Flop d_ff_7 (.clk(Clock), .D(Input[6]), .Q(out_5[6]), .en(Enable), .reset(Clear));  // open: Qn, preset
  D_Flip_Flop d_ff_8 (.clk(Clock), .D(Input[7]), .Q(out_5[7]), .en(Enable), .reset(Clear));  // open: Qn, preset
  D_Flip_Flop d_ff_9 (.clk(Clock), .D(Input[8]), .Q(out_5[8]), .en(Enable), .reset(Clear));  // open: Qn, preset
  D_Flip_Flop d_ff_10 (.clk(Clock), .D(Input[9]), .Q(out_5[9]), .en(Enable), .reset(Clear));  // open: Qn, preset
  D_Flip_Flop d_ff_11 (.clk(Clock), .D(Input[10]), .Q(out_5[10]), .en(Enable), .reset(Clear));  // open: Qn, preset
  D_Flip_Flop d_ff_12 (.clk(Clock), .D(Input[11]), .Q(out_5[11]), .en(Enable), .reset(Clear));  // open: Qn, preset
  D_Flip_Flop d_ff_13 (.clk(Clock), .D(Input[12]), .Q(out_5[12]), .en(Enable), .reset(Clear));  // open: Qn, preset
  D_Flip_Flop d_ff_14 (.clk(Clock), .D(Input[13]), .Q(out_5[13]), .en(Enable), .reset(Clear));  // open: Qn, preset
  D_Flip_Flop d_ff_15 (.clk(Clock), .D(Input[14]), .Q(out_5[14]), .en(Enable), .reset(Clear));  // open: Qn, preset
  D_Flip_Flop d_ff_16 (.clk(Clock), .D(Input[15]), .Q(out_5[15]), .en(Enable), .reset(Clear));  // open: Qn, preset

  // Other names for the same wires on the sheet: In0 = Input[0]; In1 = Input[1]; In2 = Input[2]; In3 = Input[3];
  //   In4 = Input[4]; In5 = Input[5]; In6 = Input[6]; In7 = Input[7]; In8 = Input[8]; In9 = Input[9];
  //   In10 = Input[10]; In11 = Input[11]; In12 = Input[12]; In13 = Input[13]; In14 = Input[14]; In15 = Input[15];
  //   Out0 = out_5[0]; Out1 = out_5[1]; Out2 = out_5[2]; Out3 = out_5[3]; Out4 = out_5[4]; Out5 = out_5[5];
  //   Out6 = out_5[6]; Out7 = out_5[7]; Out8 = out_5[8]; Out9 = out_5[9]; Out10 = out_5[10]; Out11 = out_5[11];
  //   Out12 = out_5[12]; Out13 = out_5[13]; Out14 = out_5[14]; Out15 = out_5[15]
endmodule

// Adder
module _16bitadder (
  input  [15:0] A,
  input  [15:0] B,
  output [15:0] Output,
  output [15:0] Zero
);

  wire n1bitadder_1_carryout, n1bitadder_2_carryout, n1bitadder_3_carryout, n1bitadder_4_carryout,
       n1bitadder_5_carryout, n1bitadder_6_carryout, n1bitadder_7_carryout, n1bitadder_8_carryout,
       n1bitadder_9_carryout, n1bitadder_10_carryout, n1bitadder_11_carryout, n1bitadder_12_carryout,
       n1bitadder_13_carryout, n1bitadder_14_carryout, n1bitadder_15_carryout;

  _1bitadder u_1bitadder_1 (.A(A[0]), .B(B[0]), .Carry_In(1'b0), .Add(Output[0]), .CarryOut(n1bitadder_1_carryout));
  _1bitadder u_1bitadder_2 (
    .A(A[1]), .B(B[1]), .Carry_In(n1bitadder_1_carryout), .Add(Output[1]), .CarryOut(n1bitadder_2_carryout));
  _1bitadder u_1bitadder_3 (
    .A(A[2]), .B(B[2]), .Carry_In(n1bitadder_2_carryout), .Add(Output[2]), .CarryOut(n1bitadder_3_carryout));
  _1bitadder u_1bitadder_4 (
    .A(A[3]), .B(B[3]), .Carry_In(n1bitadder_3_carryout), .Add(Output[3]), .CarryOut(n1bitadder_4_carryout));
  _1bitadder u_1bitadder_5 (
    .A(A[4]), .B(B[4]), .Carry_In(n1bitadder_4_carryout), .Add(Output[4]), .CarryOut(n1bitadder_5_carryout));
  _1bitadder u_1bitadder_6 (
    .A(A[5]), .B(B[5]), .Carry_In(n1bitadder_5_carryout), .Add(Output[5]), .CarryOut(n1bitadder_6_carryout));
  _1bitadder u_1bitadder_7 (
    .A(A[6]), .B(B[6]), .Carry_In(n1bitadder_6_carryout), .Add(Output[6]), .CarryOut(n1bitadder_7_carryout));
  _1bitadder u_1bitadder_8 (
    .A(A[7]), .B(B[7]), .Carry_In(n1bitadder_7_carryout), .Add(Output[7]), .CarryOut(n1bitadder_8_carryout));
  _1bitadder u_1bitadder_9 (
    .A(A[8]), .B(B[8]), .Carry_In(n1bitadder_8_carryout), .Add(Output[8]), .CarryOut(n1bitadder_9_carryout));
  _1bitadder u_1bitadder_10 (
    .A(A[9]), .B(B[9]), .Carry_In(n1bitadder_9_carryout), .Add(Output[9]), .CarryOut(n1bitadder_10_carryout));
  _1bitadder u_1bitadder_11 (
    .A(A[10]), .B(B[10]), .Carry_In(n1bitadder_10_carryout), .Add(Output[10]),
    .CarryOut(n1bitadder_11_carryout));
  _1bitadder u_1bitadder_12 (
    .A(A[11]), .B(B[11]), .Carry_In(n1bitadder_11_carryout), .Add(Output[11]),
    .CarryOut(n1bitadder_12_carryout));
  _1bitadder u_1bitadder_13 (
    .A(A[12]), .B(B[12]), .Carry_In(n1bitadder_12_carryout), .Add(Output[12]),
    .CarryOut(n1bitadder_13_carryout));
  _1bitadder u_1bitadder_14 (
    .A(A[13]), .B(B[13]), .Carry_In(n1bitadder_13_carryout), .Add(Output[13]),
    .CarryOut(n1bitadder_14_carryout));
  _1bitadder u_1bitadder_15 (
    .A(A[14]), .B(B[14]), .Carry_In(n1bitadder_14_carryout), .Add(Output[14]),
    .CarryOut(n1bitadder_15_carryout));
  _1bitadder u_1bitadder_16 (
    .A(A[15]), .B(B[15]), .Carry_In(n1bitadder_15_carryout), .Add(Output[15]));  // open: CarryOut
  assign Zero = ~{Output[15:9], Output[7], Output[8], Output[6:0]};  // NOT_Gate not_1, 16 bits wide

  // Other names for the same wires on the sheet: Atun[15:0] = A; Btun[15:0] = B; Add0 = Output[0]; Add1 = Output[1];
  //   Add2 = Output[2]; Add3 = Output[3]; Add4 = Output[4]; Add5 = Output[5]; Add6 = Output[6]; Add7 = Output[7];
  //   Add8 = Output[8]; Add9 = Output[9]; Add10 = Output[10]; Add11 = Output[11]; Add12 = Output[12];
  //   Add13 = Output[13]; Add14 = Output[14]; Add15 = Output[15]

  // Notes on the sheet:
  //   Adder
endmodule

module Type (
  input  [3:0] Opcode,
  output out_2
);

  wire I, I0, I1, I2, I3, I4, I5, I6, I7, not_1_out, R, R0, R1, R2, R3, R4, R5;

  not not_1 (not_1_out, R);
  Opcode_Decode opcode_decode_1 (
    .in_1(Opcode), .add(R0), .\not (I1), .jr(R5), .srl(R4), .addi(I0), .\xor (R2), .lw(I2), .sll(R3),
    .\input (I6), .sub(R1), .sw(I3), .blt(I5), .\output (I7), .bne(I4));  // open: jal, j
  or or_1 (R, R0, R1, R2, R3, R4, R5);
  and and_1 (out_2, not_1_out, I);
  or or_2 (I, I0, I1, I2, I3, I4, I5, I6, I7);
endmodule

// SignEx
module SignExtend (
  input  [5:0] in_1,
  output [15:0] out_2
);

  Multiplexer #(.enable("false")) multiplexer_1 (.in0(1'b0), .in1(1'b1), .out(out_2[15]), .sel(in_1[5]));

  assign out_2[14:0] = {{9{out_2[15]}}, in_1};

  // Other names for the same wires on the sheet: In0 = in_1[0]; In1 = in_1[1]; In2 = in_1[2]; In3 = in_1[3];
  //   In4 = in_1[4]; Sign = in_1[5]; _1or0 = out_2[15]
endmodule

module WriteEn (
  input  [3:0] Opcode,
  output out_2
);

  wire I0, I1, I2, I3, I4, I5, I6, I7, J0, J1, not_1_out, NoWrite, R0, R1, R2, R3, R4, R5, Write;

  not not_1 (not_1_out, Write);
  and and_1 (out_2, not_1_out, NoWrite);
  Opcode_Decode opcode_decode_1 (
    .in_1(Opcode), .add(R0), .\not (I1), .jr(R1), .srl(R2), .addi(I0), .\xor (R3), .lw(I2), .jal(J1),
    .sll(R4), .\input (I7), .sub(R5), .sw(I3), .blt(I4), .\output (I6), .bne(I5), .j(J0));
  or or_1 (Write, R0, R2, R3, R4, R5, I0, I1, I2, I7, J1);
  or or_2 (NoWrite, R1, I3, I4, I5, I6, J0);
endmodule

module ifJal (
  input  [3:0] in_1,
  output Output
);

  wire Jal, not_1_out, NotJal, opcode_decode_1_add, opcode_decode_1_addi, opcode_decode_1_blt,
       opcode_decode_1_bne, opcode_decode_1_input, opcode_decode_1_j, opcode_decode_1_jr, opcode_decode_1_lw,
       opcode_decode_1_not, opcode_decode_1_output, opcode_decode_1_sll, opcode_decode_1_srl,
       opcode_decode_1_sub, opcode_decode_1_sw, opcode_decode_1_xor;

  Opcode_Decode opcode_decode_1 (
    .in_1(in_1), .add(opcode_decode_1_add), .\not (opcode_decode_1_not), .jr(opcode_decode_1_jr),
    .srl(opcode_decode_1_srl), .addi(opcode_decode_1_addi), .\xor (opcode_decode_1_xor),
    .lw(opcode_decode_1_lw), .jal(Jal), .sll(opcode_decode_1_sll), .\input (opcode_decode_1_input),
    .sub(opcode_decode_1_sub), .sw(opcode_decode_1_sw), .blt(opcode_decode_1_blt),
    .\output (opcode_decode_1_output), .bne(opcode_decode_1_bne), .j(opcode_decode_1_j));
  not not_1 (not_1_out, NotJal);
  and and_1 (Output, not_1_out, Jal);
  or or_1 (NotJal, opcode_decode_1_add, opcode_decode_1_not, opcode_decode_1_jr, opcode_decode_1_srl, opcode_decode_1_addi, opcode_decode_1_xor, opcode_decode_1_lw, opcode_decode_1_sll, opcode_decode_1_input, opcode_decode_1_sub, opcode_decode_1_sw, opcode_decode_1_blt, opcode_decode_1_output, opcode_decode_1_bne, opcode_decode_1_j);
endmodule
